# Fritzing sketch schematic (saved by Fritzing 0.9.6b)

parts:
  Digispark1 = Digispark
  Mic1 = KY-038
  Mod1 = KY-018 Photoresistor Module [package="Breakout board"]
  S1 = Pushbutton [package="[THT]"]

nets:
  VCC: Digispark1.VCC, Mic1.pin3, Mod1.Vin
  N1: Digispark1.GND, Mic1.pin2, Mod1.-, S1.Pin_3, S1.Pin_4
  N2: Digispark1.P0, S1.Pin_1, S1.Pin_2
  N3: Digispark1.P2, Mic1.pin1
  N4: Digispark1.P5, Mod1.S

custom parts:
  Digispark: The Digispark is an Attiny85 based microcontroller development board similar to the Arduino line, only cheaper, smaller, and a bit less powerful. With a whole host of shields to extend its functionality and the ability to use the familiar Arduino IDE the Digispark is a great way to jump into electronics, or perfect for when an Arduino is too big or too much.
  KY-038: ky-038 Microphone sound sensor module
  KY-018 Photoresistor Module: KY-018 Photoresistor module, used to measure light intensity. It can determine the presence or absence of light.
